# Fritzing sketch TX_module (saved by Fritzing 0.9.3b)
breadboards: 1

parts:
  Part1 = Adafruit Feather 32u4 RFM9xW LoRa [part_number="Adafruit #3078 and Adafruit #3079"]
  868MHz_antenna = Antenna
  Q1 = 2N7000 NCH MOSFET [part_number=2n7000 package=to-92]
  U1 = Voltage Regulator - 3.3V [package="TO220 [THT]"]
  C1 = Electrolytic Capacitor [capacitance=1µF package="100 mil [THT, electrolytic]"]
  R1 = Resistor [tolerance=±5% resistance=10k package=THT]
  C2 = Electrolytic Capacitor [capacitance=10µF package="100 mil [THT, electrolytic]"]
  OLED_I2C1 = OLED 128x64 I2C Monochrome Display
  SG1 = Buzzer 12mm [part_number="3.3V/5V Buzzer" package=buzzer-ccv]

nets:
  N1: Part1.ANT, 868MHz_antenna.antenna_lead
  RX: Part1.0, R1.Pin_0
  N2: Part1.A5, SG1.2
  GND: Part1.GND, Q1.S, U1.GND, C1.-, C2.-, OLED_I2C1.GND, SG1.1
  Vcc: Part1.+3V3, U1.output_voltage, R1.Pin_1, C2.+, OLED_I2C1.VDD
  N3: Part1.3, OLED_I2C1.SCL
  N4: Part1.2, OLED_I2C1.SDA
  PPM Out: Q1.G
  Batt: U1.input_voltage, C1.+

notes:
  Taranis Bay Port

custom parts:
  Adafruit Feather 32u4 RFM9xW LoRa: This is the Adafruit Feather 32u4 LoRa Radio (RFM9x) - our take on an microcontroller with a "Long Range (LoRa)" packet radio transceiver with built in USB and battery charging. Its an Adafruit Feather 32u4 with a 868/915 MHz radio module cooked in! Great for making wireless networks that can go further than 2.4GHz 802.15.4 and similar, are more flexible than Bluetooth LE and without the high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
  2N7000 NCH MOSFET: 2N7000 NMOS footprint
